# Fritzing sketch BumpinHeart (saved by Fritzing 0.9.3b)
breadboards: 1

parts:
  BB1 = 4-Line Bi-Directional Level Shifter
  U1 = LIPO-110mAh [package=lipo-110]  # not connected
  NEOPIXEL1 = Neopixel 8x8 Matrix
  Bauteil3 = VERTER 5V USB Buck-Boost
  Bauteil4 = Adafruit Feather M0 Basic Proto [part_number="Adafruit #2772"]
  S1 = Pushbutton [package="[SMD]"]

nets:
  N1: BB1.LV, Bauteil4.+3V3
  N2: BB1.A1, Bauteil4.D12
  GND: BB1.GND#6, NEOPIXEL1.GND, Bauteil3.GND, Bauteil4.GND, S1.Pin_3, S1.Pin_4
  N3: BB1.HV, NEOPIXEL1.VCC, Bauteil3.5.0V
  N4: BB1.B1, NEOPIXEL1.DIN
  N5: Bauteil3.VIN, Bauteil4.VBAT
  N6: Bauteil3.ENABLE, Bauteil4.D10
  N7: Bauteil4.D11, S1.Pin_1, S1.Pin_2

custom parts:
  4-Line Bi-Directional Level Shifter: 4-Channel Bi-Directional Level Shifter
  Neopixel 8x8 Matrix: Adafruit Neopixel 8x8 Matrix
  VERTER 5V USB Buck-Boost: VERTER can take battery voltages from 3-12VDC and output a nice 5V DC, which makes it a perfect universal power supply for your portable project! Where Verter really shines is when you have a battery or power range that can fluctuate a lot, or you don't know what you'll end up using.
  Adafruit Feather M0 Basic Proto: At the Feather M0's heart is an ATSAMD21G18 ARM Cortex M0 processor, clocked at 48 MHz and at 3.3V logic, the same one used in the new Arduino Zero. This chip has a whopping 256K of FLASH (8x more than the Atmega328 or 32u4) and 32K of RAM (16x as much)! This chip comes with built in USB so it has USB-to-Serial program & debug capability built in with no need for an FTDI-like chip. To make it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
